# Fritzing sketch EletricScheme (saved by Fritzing 0.9.3b)

parts:
  Componente1 = Arduino Uno (Rev3)
  M1 = DC Motor
  S1 = H-Bridge with L298N
  M2 = DC Motor
  BAT1 = BC9VPC [package=bc9vpc]
  VCC1 = 4 x AAA Battery Mount  # not connected

nets:
  N1: Componente1.D8, S1.IN1
  N2: Componente1.D9_PWM, S1.ENA
  N3: Componente1.D3_PWM, S1.ENB
  N4: Componente1.D4, S1.IN4
  N5: Componente1.D5_PWM, S1.IN3
  N6: Componente1.D7, S1.IN2
  5V: Componente1.5V, S1.5V
  GND: Componente1.GND, S1.GND
  N7: M1.pin_1, S1.M2-02
  N8: M1.pin_2, S1.M2-01
  N9: S1.12V, BAT1.V+
  N10: S1.M1-01, M2.pin_2
  N11: S1.M1-02, M2.pin_1

custom parts:
  H-Bridge with L298N: h-bridge
